// Logisim project ALU Control.circ as structural Verilog: 1 circuit, main circuit ALU Control
module ALU_Control (
  input  [2:0] func,
  input  [2:0] ALUOp,
  output [3:0] ALUCtrl
);

  wire or_1_out;
  wire [3:0] multiplexer_1_out, rom_1_data, rom_2_data, rom_3_data;

  ROM #(.addrWidth(3), .dataWidth(4)) rom_1 (.addr(func), .data(rom_1_data));  // open: sel
  ROM #(.addrWidth(3), .dataWidth(4)) rom_2 (.addr(func), .data(rom_2_data));  // open: sel
  ROM #(.addrWidth(3), .dataWidth(4)) rom_3 (.addr(ALUOp), .data(rom_3_data));  // open: sel
  or or_1 (or_1_out, ALUOp[1], ALUOp[2]);
  Multiplexer #(.width(4), .enable("false")) multiplexer_1 (
    .in0(rom_1_data), .in1(rom_2_data), .out(multiplexer_1_out), .sel(ALUOp[0]));
  Multiplexer #(.width(4), .enable("false")) multiplexer_2 (
    .in0(multiplexer_1_out), .in1(rom_3_data), .out(ALUCtrl), .sel(or_1_out));

  // Notes on the sheet:
  //   contents of rom_1 (hex, n*v repeats v):
  //   0 1 2 3 c d e f
  //   contents of rom_2 (hex, n*v repeats v):
  //   4 5 8 9
  //   contents of rom_3 (hex, n*v repeats v):
  //   0 0 c d 4 8
endmodule
