// Logisim project ALU.circ as structural Verilog: 1 circuit, main circuit ALU
module ALU (
  input  [15:0] Rs,
  input  [15:0] Rt,
  input  [3:0] ALUCtrl,
  output [15:0] ALU_Output,
  output Rs_Rt
);

  wire comparator_1_lt, comparator_2_lt, multiplexer_1_out;
  wire [15:0] adder_1_out, and_1_out, bit_extender_1_out, multiplexer_2_out, multiplexer_3_out, nor_1_out,
       nor_2_out, not_1_out, shiftter_1_rd, xor_1_out;

  Comparator #(.width(16)) comparator_1 (.a(Rs), .b(Rt), .lt(comparator_1_lt));  // open: gt, eq
  Comparator #(.width(16), .mode("unsigned")) comparator_2 (
    .a(Rs), .b(Rt), .eq(Rs_Rt), .lt(comparator_2_lt));  // open: gt
  Multiplexer #(.enable("false")) multiplexer_1 (
    .in0(comparator_1_lt), .in1(comparator_2_lt), .out(multiplexer_1_out), .sel(ALUCtrl[0]));
  assign nor_1_out = ~(Rt | Rt);  // NOR_Gate nor_1, 16 bits wide
  assign and_1_out = Rs & Rt;  // AND_Gate and_1, 16 bits wide
  assign not_1_out = ~nor_2_out;  // NOT_Gate not_1, 16 bits wide
  assign nor_2_out = ~(Rs | Rt);  // NOR_Gate nor_2, 16 bits wide
  assign xor_1_out = Rs ^ Rt;  // XOR_Gate xor_1, 16 bits wide
  shiftter shiftter_1 (.Rs(Rs), .f1f0(ALUCtrl[1:0]), .Rd(shiftter_1_rd), .Rt(Rt[3:0]));
  Multiplexer #(.width(16), .enable("false")) multiplexer_2 (
    .in0(Rt), .in1(nor_1_out), .out(multiplexer_2_out), .sel(ALUCtrl[0]));
  Adder #(.width(16)) adder_1 (.a(Rs), .b(multiplexer_2_out), .out(adder_1_out), .cin(ALUCtrl[0]));  // open: cout
  assign bit_extender_1_out = {{15{1'b0}}, multiplexer_1_out};  // Bit_Extender bit_extender_1
  Multiplexer #(.select(2), .width(16), .enable("false")) multiplexer_3 (
    .in0(and_1_out), .in1(not_1_out), .in2(nor_2_out), .in3(xor_1_out), .out(multiplexer_3_out),
    .sel(ALUCtrl[1:0]));
  Multiplexer #(.select(2), .width(16), .enable("false")) multiplexer_4 (
    .in0(shiftter_1_rd), .in1(adder_1_out), .in2(bit_extender_1_out), .in3(multiplexer_3_out),
    .out(ALU_Output), .sel(ALUCtrl[3:2]));

  // Other names for the same wires on the sheet: s1s0[1:0] = ALUCtrl[1:0]
endmodule
