// Logisim project Data Path.circ as structural Verilog: 1 circuit, main circuit Data Path
module Data_Path (
);

  wire CLK, JAL, LUI, main_control_1_alusrc, main_control_1_beq, main_control_1_bne, main_control_1_extop,
       main_control_1_j, main_control_1_jr, main_control_1_memread, main_control_1_memtpreg,
       main_control_1_regdst, main_control_1_regwrite, next_pc_1_pcsrc, or_1_out, Rd__0, Rs__Rt, sw;
  wire [2:0] func, main_control_1_aluop, multiplexer_3_out, multiplexer_4_out, multiplexer_5_out,
       spliter_1_rd, spliter_1_rs, spliter_1_rt;
  wire [3:0] alu_control_1_aluctrl, Op;
  wire [5:0] Imm6;
  wire [11:0] Imm12, incrementer_1_out_2, incrementer_2_out_2, JR_Next_PC, multiplexer_1_out,
       multiplexer_2_out, next_pc_1_next_pc, PC_q;
  wire [15:0] alu_1_alu_output, bit_extender_1_out, Data, Imm6_Ext, Imm12_Ext, multiplexer_6_out,
       multiplexer_7_out, multiplexer_8_out, ram_1_data, register_file_1_rt_data, rom_1_data, shifter_1_out;
  wire [15:12] register_file_1_rs_data;

  Incrementer incrementer_1 (.in_1(PC_q), .out_2(incrementer_1_out_2));
  Multiplexer #(.width(12), .enable("false")) multiplexer_1 (
    .in0(JR_Next_PC), .in1(next_pc_1_next_pc), .out(multiplexer_1_out), .sel(main_control_1_j));
  Multiplexer #(.width(12), .enable("false")) multiplexer_2 (
    .in0(incrementer_1_out_2), .in1(multiplexer_1_out), .out(multiplexer_2_out), .sel(next_pc_1_pcsrc));
  Register #(.width(12)) PC (.D(multiplexer_2_out), .Q(PC_q), .clk(CLK));  // open: en, clr
  Next_PC next_pc_1 (
    .PC(incrementer_1_out_2), .Imm6(Imm6), .Imm12(Imm12), .PCSrc(next_pc_1_pcsrc), .Bne(main_control_1_bne),
    .Rs__Rt(Rs__Rt), .J(main_control_1_j), .Beq(main_control_1_beq), .JR(main_control_1_jr),
    .Next_PC(next_pc_1_next_pc), .Rd__0(Rd__0));
  ROM #(.addrWidth(12), .dataWidth(16)) rom_1 (.addr(PC_q), .data(rom_1_data));  // open: sel
  Sign_Extender sign_extender_1 (
    .Imm6(Imm6), .Imm12(Imm12), .out_4(Imm6_Ext), .ExtOp(main_control_1_extop), .out_5(Imm12_Ext));
  Clock clock_1 (.out(CLK));
  Spliter spliter_1 (
    .in_1(rom_1_data), .f(func), .Rt(spliter_1_rt), .Imm6(Imm6), .Rs(spliter_1_rs), .Rd(spliter_1_rd),
    .Imm12(Imm12), .Op(Op));
  Main_Control main_control_1 (
    .in_1(Op), .JR(main_control_1_jr), .LUI(LUI), .JAL(JAL), .J(main_control_1_j), .Bne(main_control_1_bne),
    .Beq(main_control_1_beq), .MemtpReg(main_control_1_memtpreg), .MemWrite(sw),
    .MemRead(main_control_1_memread), .ALUSrc(main_control_1_alusrc), .ExtOp(main_control_1_extop),
    .RegWrite(main_control_1_regwrite), .RegDst(main_control_1_regdst), .ALUOp(main_control_1_aluop));
  Multiplexer #(.width(3), .enable("false")) multiplexer_3 (
    .in0(spliter_1_rt), .in1(spliter_1_rd), .out(multiplexer_3_out), .sel(sw));
  Multiplexer #(.width(3), .enable("false")) multiplexer_4 (
    .in0(3'b001), .in1(3'b111), .out(multiplexer_4_out), .sel(JAL));
  Multiplexer #(.width(3), .enable("false")) multiplexer_5 (
    .in0(spliter_1_rd), .in1(multiplexer_4_out), .out(multiplexer_5_out), .sel(main_control_1_regdst));
  Register_File register_file_1 (
    .Rd_adrress(multiplexer_5_out), .RegWrite(main_control_1_regwrite),
    .Rs_data({register_file_1_rs_data, JR_Next_PC}), .Rt_data(register_file_1_rt_data), .Rd_data(Data),
    .Rs_address(spliter_1_rs), .Rt_address(multiplexer_3_out), .clock(CLK), .Rd__0(Rd__0));
  ALU_Control alu_control_1 (.func(func), .ALUOp(main_control_1_aluop), .ALUCtrl(alu_control_1_aluctrl));
  Multiplexer #(.width(16), .enable("false")) multiplexer_6 (
    .in0(register_file_1_rt_data), .in1(Imm6_Ext), .out(multiplexer_6_out), .sel(main_control_1_alusrc));
  ALU alu_1 (
    .Rs({register_file_1_rs_data, JR_Next_PC}), .Rt(multiplexer_6_out), .ALU_Output(alu_1_alu_output),
    .Rs_Rt(Rs__Rt), .ALUCtrl(alu_control_1_aluctrl));
  RAM #(.addrWidth(16), .dataWidth(16), .bus("separate")) ram_1 (
    .addr(alu_1_alu_output), .din(register_file_1_rt_data), .data(ram_1_data), .str(sw), .clk(CLK),
    .ld(main_control_1_memread));  // open: sel, clr
  Multiplexer #(.width(16), .enable("false")) multiplexer_7 (
    .in0(alu_1_alu_output), .in1(ram_1_data), .out(multiplexer_7_out), .sel(main_control_1_memtpreg));
  Incrementer incrementer_2 (.in_1(Imm12), .out_2(incrementer_2_out_2));
  Shifter #(.width(16)) shifter_1 (.in(Imm12_Ext), .\dist (4'b0100), .out(shifter_1_out));
  assign bit_extender_1_out = {{4{1'b0}}, incrementer_2_out_2};  // Bit_Extender bit_extender_1
  Multiplexer #(.width(16), .enable("false")) multiplexer_8 (
    .in0(bit_extender_1_out), .in1(shifter_1_out), .out(multiplexer_8_out), .sel(LUI));
  Multiplexer #(.width(16), .enable("false")) multiplexer_9 (
    .in0(multiplexer_7_out), .in1(multiplexer_8_out), .out(Data), .sel(or_1_out));
  or or_1 (or_1_out, LUI, JAL);

  // Notes on the sheet:
  //   contents of rom_1 (hex, n*v repeats v):
  //   fabc 5404 863e 1853 1a48 1c51 1e52 29c 455 65f 856 b10 d12 f13 4d1 7200 7801 6a00
endmodule
