// Logisim project Incrementer.circ as structural Verilog: 1 circuit, main circuit Incrementer
module Incrementer (
  input  [11:0] in_1,
  output [11:0] out_2
);

  Adder #(.width(12)) adder_1 (.a(in_1), .b(12'h1), .out(out_2), .cin(1'b0));  // open: cout
endmodule
