// Logisim project Main Control.circ as structural Verilog: 1 circuit, main circuit Main Control
module Main_Control (
  input  [3:0] in_1,
  output JR,
  output LUI,
  output JAL,
  output J,
  output Bne,
  output Beq,
  output MemtpReg,
  output MemWrite,
  output MemRead,
  output ALUSrc,
  output [2:0] ALUOp,
  output ExtOp,
  output RegWrite,
  output RegDst
);

  ROM #(.addrWidth(4), .dataWidth(16)) rom_1 (
    .addr(in_1),
    .data({ALUOp, RegDst, RegWrite, ExtOp, ALUSrc, MemRead, MemWrite, MemtpReg, Beq, Bne, J, JAL, LUI, JR}));  // open: sel

  // Notes on the sheet:
  //   contents of rom_1 (hex, n*v repeats v):
  //   800 2801 0 0 4a00 6a00 8f40 8680 8e00 20 ae00 10 8 1804 0 d802
endmodule
