// Logisim project Next PC.circ as structural Verilog: 1 circuit, main circuit Next PC
module Next_PC (
  input  [11:0] PC,
  input  [5:0] Imm6,
  input  [11:0] Imm12,
  input  Bne,
  input  Rs__Rt,
  input  Beq,
  input  JAL,
  input  J,
  input  JR,
  input  Rd__0,
  output PCSrc,
  output [11:0] Next_PC
);

  wire and_1_out, and_2_out, and_3_out, or_1_out;
  wire [11:0] adder_1_out, bit_extender_1_out;

  assign bit_extender_1_out = {{6{Imm6[5]}}, Imm6};  // Bit_Extender bit_extender_1
  Adder #(.width(12)) adder_1 (.a(PC), .b(bit_extender_1_out), .out(adder_1_out));  // open: cin, cout
  Multiplexer #(.width(12), .enable("false")) multiplexer_1 (
    .in0(adder_1_out), .in1(Imm12), .out(Next_PC), .sel(or_1_out));
  or or_1 (or_1_out, JAL, J);
  and and_1 (and_1_out, Bne, ~Rs__Rt);  // AND_Gate
  or or_2 (PCSrc, and_1_out, J, JAL, and_2_out, and_3_out);
  and and_2 (and_2_out, JR, Rd__0);
  and and_3 (and_3_out, Rs__Rt, Beq);
endmodule
