// Logisim project Shiftter.circ as structural Verilog: 1 circuit, main circuit shiftter
module shiftter (
  input  [15:0] Rs,
  input  [15:0] Rt,
  input  [1:0] f1f0,
  output [15:0] Rd
);

  wire [15:0] shifter_1_out, shifter_2_out, shifter_3_out, shifter_4_out;

  Shifter #(.width(16)) shifter_1 (.in(Rs), .\dist (Rt[3:0]), .out(shifter_1_out));
  Shifter #(.width(16), .shift("rl")) shifter_2 (.in(Rs), .\dist (Rt[3:0]), .out(shifter_2_out));
  Shifter #(.width(16), .shift("lr")) shifter_3 (.in(Rs), .\dist (Rt[3:0]), .out(shifter_3_out));
  Shifter #(.width(16), .shift("ar")) shifter_4 (.in(Rs), .\dist (Rt[3:0]), .out(shifter_4_out));
  Multiplexer #(.select(2), .width(16), .enable("false")) multiplexer_1 (
    .in0(shifter_1_out), .in1(shifter_2_out), .in2(shifter_3_out), .in3(shifter_4_out), .out(Rd), .sel(f1f0));

  // Other names for the same wires on the sheet: Rt_t[3:0] = Rt[3:0]
endmodule
