// Logisim project Sign Extender.circ as structural Verilog: 1 circuit, main circuit Sign Extender
module Sign_Extender (
  input  [5:0] Imm6,
  input  ExtOp,
  input  [11:0] Imm12,
  output [15:0] out_4,
  output [15:0] out_5
);

  wire [15:0] bit_extender_1_out, bit_extender_2_out, bit_extender_3_out, bit_extender_4_out;

  assign bit_extender_1_out = {{10{1'b0}}, Imm6};  // Bit_Extender bit_extender_1
  assign bit_extender_2_out = {{10{Imm6[5]}}, Imm6};  // Bit_Extender bit_extender_2
  assign bit_extender_3_out = {{4{1'b0}}, Imm12};  // Bit_Extender bit_extender_3
  assign bit_extender_4_out = {{4{Imm12[11]}}, Imm12};  // Bit_Extender bit_extender_4
  Multiplexer #(.width(16), .enable("false")) multiplexer_1 (
    .in0(bit_extender_1_out), .in1(bit_extender_2_out), .out(out_4), .sel(ExtOp));
  Multiplexer #(.width(16), .enable("false")) multiplexer_2 (
    .in0(bit_extender_3_out), .in1(bit_extender_4_out), .out(out_5), .sel(ExtOp));
endmodule
