// Logisim project Spliter.circ as structural Verilog: 1 circuit, main circuit Spliter
module Spliter (
  input  [15:0] in_1,
  output [2:0] f,
  output [2:0] Rt,
  output [5:0] Imm6,
  output [2:0] Rs,
  output [2:0] Rd,
  output [11:0] Imm12,
  output [3:0] Op
);


  assign f = in_1[2:0];
  assign Imm6 = in_1[5:0];
  assign Imm12 = in_1[11:0];
  assign Op = in_1[15:12];
  assign Rd = in_1[11:9];
  assign Rs = in_1[8:6];
  assign Rt = in_1[5:3];
endmodule
