// Logisim project alu.circ as structural Verilog: 1 circuit, main circuit main
module main (
  input  [1:0] ShiftOpSelect,
  input  [15:0] A,
  input  ArithOperation,
  input  [1:0] ALUselection,
  input  [15:0] B,
  input  SLTselect,
  input  [1:0] LogicalOp,
  output [15:0] ALUresult,
  output ZeroFlag
);

  wire comparator_1_lt, comparator_2_eq, comparator_2_lt, undriven, undriven_3;
  wire [0:0] multiplexer_2_out;
  wire [1:0] undriven_2, undriven_4, undriven_5;
  wire [15:0] adder_1_out, and_1_out, multiplexer_1_out, multiplexer_3_out, multiplexer_4_out, not_1_out,
       or_1_out, shifter_1_out, shifter_2_out, shifter_3_out, shifter_4_out, subtractor_1_out, xor_1_out;

  Shifter #(.width(16), .shift("ar")) shifter_1 (.in(A), .\dist (B[3:0]), .out(shifter_1_out));
  Shifter #(.width(16), .shift("rl")) shifter_2 (.in(A), .\dist (B[3:0]), .out(shifter_2_out));
  Shifter #(.width(16), .shift("lr")) shifter_3 (.in(A), .\dist (B[3:0]), .out(shifter_3_out));
  Shifter #(.width(16)) shifter_4 (.in(A), .\dist (B[3:0]), .out(shifter_4_out));
  Adder #(.width(16)) adder_1 (.a(A), .b(B), .out(adder_1_out));  // open: cin, cout
  Subtractor #(.width(16)) subtractor_1 (.a(A), .b(B), .out(subtractor_1_out));  // open: bin, bout
  Comparator #(.width(16)) comparator_1 (.a(A), .b(B), .lt(comparator_1_lt));  // open: gt, eq
  Comparator #(.width(16), .mode("unsigned")) comparator_2 (
    .a(A), .b(B), .eq(comparator_2_eq), .lt(comparator_2_lt));  // open: gt
  assign and_1_out = A & B;  // AND_Gate and_1, 16 bits wide
  assign or_1_out = A | B;  // OR_Gate or_1, 16 bits wide
  assign not_1_out = ~or_1_out;  // NOT_Gate not_1, 16 bits wide
  assign xor_1_out = A ^ B;  // XOR_Gate xor_1, 16 bits wide
  Multiplexer #(.width(16), .enable("false")) multiplexer_1 (
    .in0(adder_1_out), .in1(subtractor_1_out), .out(multiplexer_1_out), .sel(undriven_3));
  Multiplexer #(.enable("false")) multiplexer_2 (
    .in0(comparator_1_lt), .in1(comparator_2_lt), .out(multiplexer_2_out[0]), .sel(undriven));
  Multiplexer #(.select(2), .width(16), .enable("false")) multiplexer_3 (
    .in0(and_1_out), .in1(or_1_out), .in2(not_1_out), .in3(xor_1_out), .out(multiplexer_3_out),
    .sel(undriven_2));
  Multiplexer #(.select(2), .width(16), .enable("false")) multiplexer_4 (
    .in0(shifter_1_out), .in1(shifter_2_out), .in2(shifter_3_out), .in3(shifter_4_out),
    .out(multiplexer_4_out), .sel(undriven_4));
  Multiplexer #(.select(2), .width(16), .enable("false")) multiplexer_5 (
    .in0(multiplexer_4_out), .in1({{15{1'b0}}, multiplexer_2_out[0]}), .in2(multiplexer_1_out),
    .in3(multiplexer_3_out), .out(ALUresult), .sel(undriven_5));
  not not_2 (ZeroFlag, comparator_2_eq);

  // Notes on the sheet:
  //   SRA
  //   ROL
  //   SRL
  //   SLL
  //   Adder
  //   Subtractor
  //   Arithmatic operation
  //   SLT SELECT
  //   Shift Operation Select
  //   Logical operation
  //   ALU result
  //   ALU Selection
endmodule
