// Logisim project ALUctrl.circ as structural Verilog: 2 circuits, main circuit main
module main (
);

  ALUctrl aluctrl_1 ();  // open: ArthOp0, SLTslct0, ShiftOpSelect, LogicOp, ALUslct, OP, Func
endmodule

module ALUctrl (
  input  [3:0] OP,
  input  [2:0] Func,
  output [1:0] ShiftOpSelect,
  output ArthOp0,
  output SLTslct0,
  output [1:0] LogicOp,
  output [1:0] ALUslct
);

  wire and_4_out, and_5_out, and_6_out, and_7_out, and_8_out, and_9_out, and_10_out, and_11_out, and_12_out,
       not_1_out, not_2_out, not_3_out, not_4_out, not_5_out, not_6_out, not_7_out, not_8_out, not_9_out,
       not_10_out, not_11_out, not_12_out, not_13_out, not_14_out, not_15_out, not_16_out;

  not not_1 (not_1_out, Func[0]);
  not not_2 (not_2_out, Func[1]);
  not not_3 (not_3_out, OP[2]);
  not not_4 (not_4_out, OP[1]);
  not not_5 (not_5_out, OP[2]);
  not not_6 (not_6_out, OP[2]);
  not not_7 (not_7_out, OP[1]);
  not not_8 (not_8_out, OP[2]);
  not not_9 (not_9_out, Func[1]);
  not not_10 (not_10_out, OP[3]);
  not not_11 (not_11_out, OP[1]);
  not not_12 (not_12_out, OP[3]);
  not not_13 (not_13_out, OP[1]);
  not not_14 (not_14_out, OP[2]);
  not not_15 (not_15_out, OP[2]);
  not not_16 (not_16_out, OP[1]);
  or or_1 (ShiftOpSelect[1], not_1_out, OP[2]);
  or or_2 (ShiftOpSelect[0], not_2_out, OP[2]);
  and and_1 (ArthOp0, not_3_out, OP[0], Func[0]);
  and and_2 (SLTslct0, not_4_out, Func[0]);
  and and_3 (LogicOp[1], not_5_out, Func[1]);
  and and_4 (and_4_out, not_6_out, Func[0]);
  and and_5 (and_5_out, not_7_out, Func[2]);
  and and_6 (and_6_out, not_8_out, OP[0], not_9_out);
  and and_7 (and_7_out, not_10_out, OP[2]);
  and and_8 (and_8_out, OP[3], not_11_out);
  and and_9 (and_9_out, not_12_out, not_13_out, Func[2]);
  and and_10 (and_10_out, not_14_out, OP[0], Func[1]);
  and and_11 (and_11_out, not_15_out, OP[1]);
  and and_12 (and_12_out, OP[2], not_16_out);
  or or_3 (LogicOp[0], and_4_out, OP[0]);
  or or_4 (ALUslct[1], and_5_out, and_6_out, and_7_out, and_8_out);
  or or_5 (ALUslct[0], and_9_out, and_10_out, and_11_out, and_12_out);
endmodule
