// Logisim project MainControlUnit.circ as structural Verilog: 1 circuit, main circuit main
module main (
  input  [3:0] OP,
  input  [2:0] in_2,
  output LUI,
  output BusWslct,
  output RegWrite,
  output Beg,
  output j,
  output Bne,
  output ALUscr,
  output RegDest,
  output SWslct,
  output JAL,
  output JR
);

  wire and_4_out, and_8_out, and_9_out;

  and and_1 (LUI, OP[3], OP[2], OP[1], OP[0]);
  and and_2 (BusWslct, ~OP[3], OP[2], OP[1], ~OP[0]);  // AND_Gate
  and and_3 (Beg, OP[3], ~OP[2], ~OP[1], OP[0]);  // AND_Gate
  and and_4 (and_4_out, OP[3], OP[2], ~OP[1], ~OP[0]);  // AND_Gate
  and and_5 (Bne, OP[3], ~OP[2], OP[1], OP[0]);  // AND_Gate
  and and_6 (SWslct, ~OP[3], OP[2], OP[1], OP[0]);  // AND_Gate
  and and_7 (JAL, OP[3], OP[2], ~OP[1], OP[0]);  // AND_Gate
  or or_1 (j, and_4_out, JR, JAL);
  and and_8 (and_8_out, ~OP[3], ~OP[2], ~OP[1]);  // AND_Gate
  and and_9 (and_9_out, ~Beg, ~and_4_out, ~Bne, ~SWslct);  // AND_Gate
  not not_1 (RegDest, and_8_out);
  and and_10 (JR, and_8_out, in_2[0], in_2[1], in_2[2]);
  and and_11 (RegWrite, and_9_out, ~JR);  // AND_Gate
  nor nor_1 (ALUscr, Beg, Bne, and_8_out);
endmodule
