// Logisim project SC.circ as structural Verilog: 1 circuit, main circuit main
module main (
);

  wire aluctrl_1_arthop0, aluctrl_1_sltslct0, clock_1_out, main_2_aluscr, main_2_beg, main_2_bne,
       main_2_buswslct, main_2_j, main_2_jal, main_2_jr, main_2_lui, main_2_regdest, main_2_regwrite,
       main_2_swslct, main_4_pcsrc, main_5_zeroflag;
  wire [1:0] aluctrl_1_aluslct, aluctrl_1_logicop, aluctrl_1_shiftopselect;
  wire [2:0] main_1_func, main_1_rd, main_1_rs, main_1_rt, multiplexer_2_out, multiplexer_3_out,
       multiplexer_4_out;
  wire [3:0] main_1_op;
  wire [5:0] main_1_imm6;
  wire [11:0] adder_1_out, main_1_imm12, main_4_branch_or_jump_target_address, multiplexer_1_out,
       multiplexer_6_out, PC_q;
  wire [15:0] bit_extender_1_out, bit_extender_2_out, bit_extender_3_out, main_3_busa, main_3_busb,
       main_5_aluresult, multiplexer_5_out, multiplexer_7_out, multiplexer_8_out, multiplexer_9_out,
       multiplexer_10_out, ram_1_data, rom_1_data;

  Clock clock_1 (.out(clock_1_out));
  Multiplexer #(.width(12), .enable("false")) multiplexer_1 (
    .in0(adder_1_out), .in1(main_4_branch_or_jump_target_address), .out(multiplexer_1_out), .sel(main_4_pcsrc));
  Register #(.width(12)) PC (.D(multiplexer_1_out), .Q(PC_q), .clk(clock_1_out), .clr(1'b0));  // open: en
  Adder #(.width(12)) adder_1 (.a(12'h1), .b(PC_q), .out(adder_1_out));  // open: cin, cout
  ROM #(.addrWidth(12), .dataWidth(16)) rom_1 (.addr(PC_q), .data(rom_1_data), .sel(1'b1));
  splitter_main main_1 (
    .DataInput(rom_1_data), .Rs(main_1_rs), .OP(main_1_op), .Imm12(main_1_imm12), .Imm6(main_1_imm6),
    .Func(main_1_func), .Rd(main_1_rd), .Rt(main_1_rt));
  assign bit_extender_1_out = {{4{1'b0}}, adder_1_out};  // Bit_Extender bit_extender_1
  Multiplexer #(.width(3), .enable("false")) multiplexer_2 (
    .in0(main_1_rd), .in1(main_1_rt), .out(multiplexer_2_out), .sel(main_2_regdest));
  Multiplexer #(.width(3), .enable("false")) multiplexer_3 (
    .in0(multiplexer_2_out), .in1(3'b111), .out(multiplexer_3_out), .sel(main_2_jal));
  Multiplexer #(.width(3), .enable("false")) multiplexer_4 (
    .in0(multiplexer_3_out), .in1(3'b001), .out(multiplexer_4_out), .sel(main_2_lui));
  Multiplexer #(.width(16), .enable("false")) multiplexer_5 (
    .in0(multiplexer_10_out), .in1(bit_extender_1_out), .out(multiplexer_5_out), .sel(main_2_jal));
  assign bit_extender_2_out = {{4{1'b0}}, main_1_imm12};  // Bit_Extender bit_extender_2
  MainControlUnit_main main_2 (
    .OP(main_1_op), .BusWslct(main_2_buswslct), .Beg(main_2_beg), .j(main_2_j), .Bne(main_2_bne),
    .ALUscr(main_2_aluscr), .RegDest(main_2_regdest), .SWslct(main_2_swslct), .RegWrite(main_2_regwrite),
    .JAL(main_2_jal), .in_2(main_1_func), .JR(main_2_jr), .LUI(main_2_lui));
  RF_02_main main_3 (
    .RA(main_1_rs), .RB(main_1_rt), .RW(multiplexer_4_out), .BusW(multiplexer_5_out),
    .RegWrite(main_2_regwrite), .BusA(main_3_busa), .BusB(main_3_busb), .in_6(clock_1_out));
  Multiplexer #(.width(12), .enable("false")) multiplexer_6 (
    .in0(main_1_imm12), .in1(main_3_busa[11:0]), .out(multiplexer_6_out), .sel(main_2_jr));
  assign bit_extender_3_out = {{10{1'b0}}, main_1_imm6};  // Bit_Extender bit_extender_3
  Multiplexer #(.width(16), .enable("false")) multiplexer_7 (
    .in0(main_3_busa), .in1(bit_extender_2_out), .out(multiplexer_7_out), .sel(main_2_lui));
  Multiplexer #(.width(16), .enable("false")) multiplexer_8 (
    .in0(main_3_busb), .in1(bit_extender_3_out), .out(multiplexer_8_out), .sel(main_2_aluscr));
  ALUctrl aluctrl_1 (
    .ArthOp0(aluctrl_1_arthop0), .SLTslct0(aluctrl_1_sltslct0), .ShiftOpSelect(aluctrl_1_shiftopselect),
    .LogicOp(aluctrl_1_logicop), .ALUslct(aluctrl_1_aluslct), .OP(main_1_op), .Func(main_1_func));
  next_PC_01_main main_4 (
    .Inc_PC(adder_1_out), .imm12(multiplexer_6_out),
    .Branch_or_Jump_Target_Address(main_4_branch_or_jump_target_address), .PCSrc(main_4_pcsrc),
    .BEQ(main_2_beg), .BNE(main_2_bne), .J(main_2_j), .ZERO(main_5_zeroflag));
  Multiplexer #(.width(16), .enable("false")) multiplexer_9 (
    .in0(multiplexer_8_out), .in1(16'h4), .out(multiplexer_9_out), .sel(main_2_lui));
  alu_main main_5 (
    .ShiftOpSelect(aluctrl_1_shiftopselect), .ArithOperation(aluctrl_1_arthop0),
    .ALUselection(aluctrl_1_aluslct), .SLTselect(aluctrl_1_sltslct0), .LogicalOp(aluctrl_1_logicop),
    .ZeroFlag(main_5_zeroflag), .ALUresult(main_5_aluresult), .B(multiplexer_9_out), .A(multiplexer_7_out));
  RAM #(.addrWidth(16), .dataWidth(16), .bus("separate")) ram_1 (
    .addr(main_5_aluresult), .din(main_3_busb), .data(ram_1_data), .str(main_2_swslct), .sel(1'b1),
    .clk(clock_1_out), .ld(main_2_buswslct), .clr(1'b0));
  Multiplexer #(.width(16), .enable("false")) multiplexer_10 (
    .in0(main_5_aluresult), .in1(ram_1_data), .out(multiplexer_10_out), .sel(main_2_buswslct));

  // Notes on the sheet:
  //   contents of rom_1 (hex, n*v repeats v):
  //   8041 8082 1298 faab 7440
endmodule
