// Logisim project next PC.01.circ as structural Verilog: 1 circuit, main circuit main
module main (
  input  [11:0] Inc_PC,
  input  [11:0] imm12,
  input  BEQ,
  input  BNE,
  input  J,
  input  ZERO,
  output [11:0] Branch_or_Jump_Target_Address,
  output PCSrc
);

  wire and_1_out, and_2_out;
  wire [11:0] adder_1_out, bit_extender_1_out;

  assign bit_extender_1_out = {{6{1'b0}}, imm12[5:0]};  // Bit_Extender bit_extender_1
  Adder #(.width(12)) adder_1 (.a(Inc_PC), .b(bit_extender_1_out), .out(adder_1_out));  // open: cin, cout
  Multiplexer #(.width(12), .enable("false")) multiplexer_1 (
    .in0(adder_1_out), .in1(imm12), .out(Branch_or_Jump_Target_Address), .sel(J));
  and and_1 (and_1_out, ~ZERO, BNE);  // AND_Gate
  or or_1 (PCSrc, and_1_out, J, and_2_out);
  and and_2 (and_2_out, ZERO, BEQ);
endmodule
