// Logisim project splitter.circ as structural Verilog: 1 circuit, main circuit main
module main (
  input  [15:0] DataInput,
  output [3:0] OP,
  output [11:0] Imm12,
  output [5:0] Imm6,
  output [2:0] Func,
  output [2:0] Rd,
  output [2:0] Rt,
  output [2:0] Rs
);


  assign Func = DataInput[2:0];
  assign Imm6 = DataInput[5:0];
  assign Imm12 = DataInput[11:0];
  assign OP = DataInput[15:12];
  assign Rd = DataInput[5:3];
  assign Rs = DataInput[11:9];
  assign Rt = DataInput[8:6];
endmodule
